// Logisim project projeto_2.circ as structural Verilog: 1 circuit, main circuit main
module main (
);

  wire and_1_out, and_2_out, or_1_out, undriven, undriven_2, undriven_3, undriven_4;

  and and_1 (and_1_out, undriven, undriven_2, undriven_3);
  or or_1 (or_1_out, undriven, undriven_2);
  and and_2 (and_2_out, or_1_out, undriven_4);
  // OR_Gate or_2 has open pins: in0=and_1_out, in4=and_2_out, out=open

  // Notes on the sheet:
  //   A
  //   B
  //   C
  //   a+b
  //   (A.B.C
  //   S = (A.B.C) + (A.B).C
  //   (A+B)C
endmodule
