// Logisim project projeto_3circ.circ as structural Verilog: 1 circuit, main circuit main
module main (
);

  wire controlled_inverter_1_out, controlled_inverter_2_out, nor_1_out, nor_2_out, not_1_out, or_1_out,
       undriven, undriven_2, undriven_3, undriven_4, undriven_5;

  Controlled_Inverter controlled_inverter_1 (.in(undriven), .out(controlled_inverter_1_out));  // open: en
  Controlled_Inverter controlled_inverter_2 (.in(undriven_3), .out(controlled_inverter_2_out));  // open: en
  not nor_1 (nor_1_out, undriven_2);  // NOR_Gate
  nor nor_2 (nor_2_out, controlled_inverter_2_out, undriven_4);
  or or_1 (or_1_out, nor_1_out, nor_2_out);
  not not_1 (not_1_out, undriven_4);
  // AND_Gate and_1 has open pins: in0=or_1_out, in1=not_1_out, in3=undriven_5, out=open

  // Notes on the sheet:
  //   a
  //   B
  //   C
  //   D
  //   S = [(a'+b)' + (c'+d)' . d'
  //   S
endmodule
