// Logisim project projeto_1 diego maia fernandes.circ as structural Verilog: 1 circuit, main circuit main
module main (
);

  wire and_1_out, and_2_out, undriven, undriven_2, undriven_3, undriven_4, xor_1_out;

  and and_1 (and_1_out, undriven, undriven_2, undriven_3);
  ExactlyOne xor_1 (.out(xor_1_out), .in1(and_1_out), .in2(undriven), .in3(undriven_3));
  and and_2 (and_2_out, xor_1_out, undriven_4);

  // Notes on the sheet:
  //   A
  //   B
  //   C
  //   D
  //   Expressão Algebrica
  //   x = (((A.B.C) (+) A(x)C). D')
  //   x
endmodule
